# Fritzing sketch estacionamento-hardware-vaga (saved by Fritzing 0.9.3b)
breadboards: 1

parts:
  Arduino1 = Arduino Mini (Rev5)
  hc-sr1 = hc-sr04
  HC-1 = HC-12 Module
  Antenna1 = HC-12 Antenna  # not connected

nets:
  GND: Arduino1.GND, hc-sr1.GND, HC-1.GND
  VCC: Arduino1.5V, hc-sr1.VCC, HC-1.VCC
  N1: Arduino1.D13, hc-sr1.Echo
  N2: Arduino1.D12, hc-sr1.Trig
  N3: Arduino1.D11_PWM, HC-1.RXD
  N4: Arduino1.D10_PWM, HC-1.TXD

custom parts:
  HC-12 Module: HC-12 433Mhz Module
  HC-12 Antenna: Antenna for HC-12 433Mhz Module
